// Logisim project 2-bitCounter.circ as structural Verilog: 2 circuits, main circuit main
module main (
  input  in_1
);

  wire n2bitcounter_1_overflow, n2bitcounter_2_overflow;
  wire [3:0] n2bitcounter_1_output0;

  _2bitCounter u_2bitcounter_1 (
    .X(in_1), .Output0(n2bitcounter_1_output0[0]), .Output1(n2bitcounter_1_output0[1]),
    .Overflow(n2bitcounter_1_overflow));
  _2bitCounter u_2bitcounter_2 (
    .X(n2bitcounter_1_overflow), .Output0(n2bitcounter_1_output0[2]), .Output1(n2bitcounter_1_output0[3]),
    .Overflow(n2bitcounter_2_overflow));
  Hex_Digit_Display hex_digit_display_1 (.value(n2bitcounter_1_output0), .dp(n2bitcounter_2_overflow));
endmodule

module _2bitCounter (
  input  X,
  output Output0,
  output Output1,
  output Overflow
);

  wire and_1_out, and_2_out, and_3_out, and_4_out, and_5_out, clock_1_out, not_1_out, not_2_out, not_3_out,
       or_1_out, or_2_out;

  not not_1 (not_1_out, X);
  not not_2 (not_2_out, Output0);
  not not_3 (not_3_out, Output1);
  and and_1 (and_1_out, Output0, not_1_out);
  and and_2 (and_2_out, not_2_out, X);
  and and_3 (and_3_out, not_2_out, Output1);
  and and_4 (and_4_out, Output1, not_1_out);
  and and_5 (and_5_out, not_3_out, Output0, X);
  or or_1 (or_1_out, and_1_out, and_2_out);
  or or_2 (or_2_out, and_3_out, and_4_out, and_5_out);
  Clock clock_1 (.out(clock_1_out));
  D_Flip_Flop B (.clk(clock_1_out), .D(or_1_out), .Q(Output0));  // open: Qn, preset, en, reset
  D_Flip_Flop A (.clk(clock_1_out), .D(or_2_out), .Q(Output1));  // open: Qn, preset, en, reset
  and and_6 (Overflow, Output0, Output1, X);
endmodule
