// Logisim project 4-bit sequence counter.circ as structural Verilog: 1 circuit, main circuit 4-bit sequence counter
// counter
module _4_bit_sequence_counter (
  input  INC,
  input  CLC,
  input  CLR,
  output [3:0] Output
);

  wire buffer_1_out, register_2_q;
  wire [3:0] adder_1_out;

  Register #(.width(4)) register_1 (.D(adder_1_out), .en(INC), .Q(Output), .clk(CLC), .clr(register_2_q));
  Adder #(.width(4)) adder_1 (.a(Output), .b(4'b0001), .out(adder_1_out));  // open: cin, cout
  Register #(.width(1)) register_2 (.D(CLR), .Q(register_2_q), .clk(CLC), .clr(buffer_1_out));  // open: en
  buf buffer_1 (buffer_1_out, CLC);
endmodule
