// Logisim project 4_bit_up_down_ripple_counter.circ as structural Verilog: 2 circuits, main circuit main
module main (
  input  Input
);

  wire and_1_out, and_2_out, clock_1_out, multiplexer_1_out, multiplexer_2_out, multiplexer_3_out, nor_1_out,
       nor_2_out, not_1_out, not_2_out;
  wire [3:0] t_ff_1_q;

  nor nor_1 (nor_1_out, t_ff_1_q[0], t_ff_1_q[1]);
  not not_1 (not_1_out, nor_1_out);
  nor nor_2 (nor_2_out, not_1_out, t_ff_1_q[2]);
  not not_2 (not_2_out, t_ff_1_q[0]);
  and and_1 (and_1_out, t_ff_1_q[0], t_ff_1_q[1]);
  and and_2 (and_2_out, and_1_out, t_ff_1_q[2]);
  Multiplexer #(.enable("false")) multiplexer_1 (
    .in0(and_1_out), .in1(nor_1_out), .out(multiplexer_1_out), .sel(Input));
  Multiplexer #(.enable("false")) multiplexer_2 (
    .in0(and_2_out), .in1(nor_2_out), .out(multiplexer_2_out), .sel(Input));
  Clock clock_1 (.out(clock_1_out));
  Multiplexer #(.enable("false")) multiplexer_3 (
    .in0(t_ff_1_q[0]), .in1(not_2_out), .out(multiplexer_3_out), .sel(Input));
  T_Flip_Flop t_ff_1 (.clk(clock_1_out), .T(1'b1), .Q(t_ff_1_q[0]));  // open: Qn, preset, reset, en
  T_Flip_Flop t_ff_2 (.clk(clock_1_out), .T(multiplexer_3_out), .Q(t_ff_1_q[1]));  // open: Qn, preset, reset, en
  T_Flip_Flop t_ff_3 (.clk(clock_1_out), .T(multiplexer_1_out), .Q(t_ff_1_q[2]));  // open: Qn, preset, reset, en
  T_Flip_Flop t_ff_4 (.clk(clock_1_out), .T(multiplexer_2_out), .Q(t_ff_1_q[3]));  // open: Qn, preset, reset, en
  Hex_Digit_Display hex_digit_display_1 (.value(t_ff_1_q));  // open: dp

  // Notes on the sheet:
  //   Output
endmodule

module CounterWithEnable (
  input  Input,
  input  Enable
);

  wire and_1_out, and_2_out, clock_1_out, multiplexer_1_out, multiplexer_2_out, multiplexer_3_out,
       multiplexer_4_out, multiplexer_5_out, multiplexer_6_out, multiplexer_7_out, nor_1_out, nor_2_out,
       not_1_out, not_2_out;
  wire [3:0] t_ff_1_q;

  nor nor_1 (nor_1_out, t_ff_1_q[0], t_ff_1_q[1]);
  not not_1 (not_1_out, nor_1_out);
  nor nor_2 (nor_2_out, not_1_out, t_ff_1_q[2]);
  not not_2 (not_2_out, t_ff_1_q[0]);
  and and_1 (and_1_out, t_ff_1_q[0], t_ff_1_q[1]);
  and and_2 (and_2_out, and_1_out, t_ff_1_q[2]);
  Multiplexer #(.enable("false")) multiplexer_1 (
    .in0(and_1_out), .in1(nor_1_out), .out(multiplexer_1_out), .sel(Input));
  Multiplexer #(.enable("false")) multiplexer_2 (
    .in0(and_2_out), .in1(nor_2_out), .out(multiplexer_2_out), .sel(Input));
  Multiplexer #(.enable("false")) multiplexer_3 (
    .in0(t_ff_1_q[0]), .in1(not_2_out), .out(multiplexer_3_out), .sel(Input));
  Clock clock_1 (.out(clock_1_out));
  Multiplexer #(.enable("false")) multiplexer_4 (.in0(1'b0), .in1(1'b1), .out(multiplexer_4_out), .sel(Enable));
  Multiplexer #(.enable("false")) multiplexer_5 (
    .in0(1'b0), .in1(multiplexer_3_out), .out(multiplexer_5_out), .sel(Enable));
  Multiplexer #(.enable("false")) multiplexer_6 (
    .in0(1'b0), .in1(multiplexer_1_out), .out(multiplexer_6_out), .sel(Enable));
  Multiplexer #(.enable("false")) multiplexer_7 (
    .in0(1'b0), .in1(multiplexer_2_out), .out(multiplexer_7_out), .sel(Enable));
  T_Flip_Flop t_ff_1 (.clk(clock_1_out), .T(multiplexer_4_out), .Q(t_ff_1_q[0]));  // open: Qn, preset, reset, en
  T_Flip_Flop t_ff_2 (.clk(clock_1_out), .T(multiplexer_5_out), .Q(t_ff_1_q[1]));  // open: Qn, preset, reset, en
  T_Flip_Flop t_ff_3 (.clk(clock_1_out), .T(multiplexer_6_out), .Q(t_ff_1_q[2]));  // open: Qn, preset, reset, en
  T_Flip_Flop t_ff_4 (.clk(clock_1_out), .T(multiplexer_7_out), .Q(t_ff_1_q[3]));  // open: Qn, preset, reset, en
  Hex_Digit_Display hex_digit_display_1 (.value(t_ff_1_q));  // open: dp

  // Notes on the sheet:
  //   Simply, connect "Enable"
  //   Output
endmodule
