// Logisim project 040100117_hw1.circ as structural Verilog: 1 circuit, main circuit main
module main (
  input  X
);

  wire clock_1_out;
  wire [3:0] LSB_q, multiplexer_1_out, not_1_out;

  Clock clock_1 (.out(clock_1_out));
  T_Flip_Flop LSB (.clk(clock_1_out), .T(1'b1), .Q(LSB_q[0]));  // open: Qn, preset, reset, en
  T_Flip_Flop t_ff_1 (.clk(LSB_q[0]), .T(1'b1), .Q(LSB_q[1]));  // open: Qn, preset, reset, en
  T_Flip_Flop t_ff_2 (.clk(LSB_q[1]), .T(1'b1), .Q(LSB_q[2]));  // open: Qn, preset, reset, en
  T_Flip_Flop MSB (.clk(LSB_q[2]), .T(1'b1), .Q(LSB_q[3]));  // open: Qn, preset, reset, en
  assign not_1_out = ~LSB_q;  // NOT_Gate not_1, 4 bits wide
  Hex_Digit_Display hex_digit_display_1 (.value(multiplexer_1_out));  // open: dp
  Multiplexer #(.width(4), .enable("false")) multiplexer_1 (
    .in0(not_1_out), .in1(LSB_q), .out(multiplexer_1_out), .sel(X));
endmodule
