// Logisim project 040100117_hw2.circ as structural Verilog: 2 circuits, main circuit main
module main (
);

  wire clock_1_out;
  wire [3:0] n4_bit_counter_1_output;
  wire [7:0] adder_1_out, ram_1_data, register_1_q;

  Clock clock_1 (.out(clock_1_out));
  _4_Bit_Counter u_4_bit_counter_1 (.Clock(clock_1_out), .Output(n4_bit_counter_1_output));
  RAM #(.addrWidth(4)) ram_1 (
    .addr(n4_bit_counter_1_output), .data(ram_1_data), .clk(clock_1_out));  // open: sel, ld, clr
  Adder adder_1 (.a(register_1_q), .b(ram_1_data), .out(adder_1_out));  // open: cin, cout
  Register register_1 (.D(adder_1_out), .Q(register_1_q), .clk(clock_1_out));  // open: en, clr
endmodule

module _4_Bit_Counter (
  input  Clock,
  output [3:0] Output
);

  wire LSB_q, t_ff_1_q, t_ff_2_q;

  T_Flip_Flop LSB (.clk(Clock), .T(1'b1), .Q(LSB_q), .Qn(Output[0]));  // open: preset, reset, en
  T_Flip_Flop t_ff_1 (.clk(LSB_q), .T(1'b1), .Q(t_ff_1_q), .Qn(Output[1]));  // open: preset, reset, en
  T_Flip_Flop t_ff_2 (.clk(t_ff_1_q), .T(1'b1), .Q(t_ff_2_q), .Qn(Output[2]));  // open: preset, reset, en
  T_Flip_Flop MSB (.clk(t_ff_2_q), .T(1'b1), .Qn(Output[3]));  // open: Q, preset, reset, en
  Hex_Digit_Display hex_digit_display_1 (.value(Output));  // open: dp
endmodule
