// Logisim project ripple.circ as structural Verilog: 2 circuits, main circuit main
module main (
  input  in_1
);

  wire clock_1_out, multiplexer_1_out, multiplexer_2_out, multiplexer_3_out, t_ff_1_qn, t_ff_2_qn, t_ff_3_qn;
  wire [3:0] t_ff_1_q;

  Clock clock_1 (.out(clock_1_out));
  T_Flip_Flop t_ff_1 (.clk(clock_1_out), .T(1'b1), .Q(t_ff_1_q[0]), .Qn(t_ff_1_qn));  // open: preset, reset, en
  T_Flip_Flop t_ff_2 (.clk(multiplexer_1_out), .T(1'b1), .Q(t_ff_1_q[1]), .Qn(t_ff_2_qn));  // open: preset, reset, en
  T_Flip_Flop t_ff_3 (.clk(multiplexer_2_out), .T(1'b1), .Q(t_ff_1_q[2]), .Qn(t_ff_3_qn));  // open: preset, reset, en
  T_Flip_Flop t_ff_4 (.clk(multiplexer_3_out), .T(1'b1), .Q(t_ff_1_q[3]));  // open: Qn, preset, reset, en
  Multiplexer #(.enable("false")) multiplexer_1 (
    .in0(t_ff_1_qn), .in1(t_ff_1_q[0]), .out(multiplexer_1_out), .sel(in_1));
  Multiplexer #(.enable("false")) multiplexer_2 (
    .in0(t_ff_2_qn), .in1(t_ff_1_q[1]), .out(multiplexer_2_out), .sel(in_1));
  Multiplexer #(.enable("false")) multiplexer_3 (
    .in0(t_ff_3_qn), .in1(t_ff_1_q[2]), .out(multiplexer_3_out), .sel(in_1));
  Hex_Digit_Display hex_digit_display_1 (.value(t_ff_1_q));  // open: dp
endmodule

module rippleCounter (
  input  Enable
);

  wire clock_1_out, t_ff_1_qn, t_ff_2_qn, t_ff_3_qn;
  wire [3:0] t_ff_1_q;

  Clock clock_1 (.out(clock_1_out));
  T_Flip_Flop t_ff_1 (
    .clk(clock_1_out), .T(1'b1), .Q(t_ff_1_q[0]), .Qn(t_ff_1_qn), .en(Enable));  // open: preset, reset
  T_Flip_Flop t_ff_2 (.clk(t_ff_1_qn), .T(1'b1), .Q(t_ff_1_q[1]), .Qn(t_ff_2_qn), .en(Enable));  // open: preset, reset
  T_Flip_Flop t_ff_3 (.clk(t_ff_2_qn), .T(1'b1), .Q(t_ff_1_q[2]), .Qn(t_ff_3_qn), .en(Enable));  // open: preset, reset
  T_Flip_Flop t_ff_4 (.clk(t_ff_3_qn), .T(1'b1), .Q(t_ff_1_q[3]), .en(Enable));  // open: Qn, preset, reset
  Hex_Digit_Display hex_digit_display_1 (.value(t_ff_1_q));  // open: dp
endmodule
