// Logisim project devr.circ as structural Verilog
module _1a (
  input  A,
  input  B,
  output A_2
);

  wire and_1_out;

  and and_1 (and_1_out, A, B);
  or or_1 (A_2, A, and_1_out);

  // Notes on the sheet:
  //   2
  //   3
  //   1
  //   7408
  //   74LS32
  //   2
  //   3
  //   1
endmodule

module _3a (
  input  X,
  input  Y,
  input  Z,
  output F
);

  wire and_1_out;

  and and_1 (and_1_out, Y, Z);
  or or_1 (F, X, and_1_out);

  // Notes on the sheet:
  //   2
  //   1
  //   7408
  //   74LS32
  //   2
  //   1
  //   3
  //   3
endmodule

module _4 (
  input  A,
  input  B,
  input  C,
  input  D,
  output F
);

  wire and_1_out, not_1_out, not_2_out, not_3_out;

  not not_1 (not_1_out, B);
  not not_2 (not_2_out, C);
  not not_3 (not_3_out, D);
  and and_1 (and_1_out, not_1_out, not_2_out);
  or or_1 (F, and_1_out, not_3_out);

  // Notes on the sheet:
  //   5
  //   3
  //   1
  //   7404
  //   7408
  //   2
  //   6
  //   4
  //   1
  //   2
  //   3
  //   2
  //   1
  //   74LS32
  //   3
endmodule

module _1b (
  input  A,
  input  B,
  output A_2
);

  wire or_1_out;

  or or_1 (or_1_out, A, B);
  and and_1 (A_2, A, or_1_out);

  // Notes on the sheet:
  //   2
  //   1
  //   74LS32
  //   7408
  //   2
  //   3
  //   1
  //   3
endmodule

module _2 (
  input  A,
  input  B,
  output A_2
);

  wire not_1_out, or_1_out, or_2_out;

  not not_1 (not_1_out, B);
  or or_1 (or_1_out, A, B);
  or or_2 (or_2_out, A, not_1_out);
  and and_1 (A_2, or_1_out, or_2_out);

  // Notes on the sheet:
  //   1
  //   7404
  //   74LS32
  //   5
  //   4
  //   2
  //   2
  //   1
  //   74LS32
  //   6
  //   7408
  //   2
  //   1
  //   3
  //   3
endmodule

module _3b (
  input  X,
  input  Y,
  input  Z,
  output F_prime
);

  wire not_1_out, not_2_out, not_3_out, or_1_out;

  not not_1 (not_1_out, X);
  not not_2 (not_2_out, Y);
  not not_3 (not_3_out, Z);
  or or_1 (or_1_out, not_2_out, not_3_out);
  and and_1 (F_prime, not_1_out, or_1_out);

  // Notes on the sheet:
  //   5
  //   3
  //   1
  //   6
  //   4
  //   2
  //   2
  //   1
  //   7404
  //   2
  //   1
  //   3
  //   74LS32
  //   7408
  //   3
endmodule
