// Logisim project 1.circ as structural Verilog: 1 circuit, main circuit main
module main (
  input  A,
  input  B,
  input  C,
  input  D,
  output F
);

  wire and_1_out, and_2_out, and_3_out, and_4_out, not_1_out, not_2_out, not_3_out, not_4_out, or_1_out,
       or_2_out;

  not not_1 (not_1_out, C);
  not not_2 (not_2_out, B);
  not not_3 (not_3_out, C);
  not not_4 (not_4_out, D);
  and and_1 (and_1_out, B, D);
  and and_2 (and_2_out, C, D);
  and and_3 (and_3_out, A, B, not_1_out);
  and and_4 (and_4_out, not_2_out, not_3_out, not_4_out);
  or or_1 (or_1_out, and_1_out, and_2_out);
  or or_2 (or_2_out, and_3_out, and_4_out);
  or or_3 (F, or_1_out, or_2_out);

  // Notes on the sheet:
  //   13
  //   12
  //   6
  //   5
  //   3
  //   4
  //   1
  //   2
  //   7404
  //   5
  //   4
  //   7408
  //   2
  //   1
  //   7408
  //   5
  //   4
  //   6
  //   3
  //   7411
  //   13
  //   2
  //   12
  //   1
  //   7411
  //   6
  //   5
  //   4
  //   3
  //   7432
  //   2
  //   1
  //   7432
  //   6
  //   12
  //   13
  //   3
  //   11
  //   7432
endmodule
