// Logisim project 2.circ as structural Verilog: 1 circuit, main circuit main
module main (
  input  A,
  input  B,
  input  C,
  input  D,
  output F
);

  wire nand_1_out, nand_2_out, nand_3_out, nand_4_out, nand_5_out, nand_6_out, not_1_out, not_2_out,
       not_3_out, not_4_out, not_5_out, not_6_out;

  not not_1 (not_1_out, C);
  not not_2 (not_2_out, B);
  not not_3 (not_3_out, C);
  not not_4 (not_4_out, D);
  nand nand_1 (nand_1_out, B, D);
  nand nand_2 (nand_2_out, C, D);
  nand nand_3 (nand_3_out, A, B, not_1_out);
  nand nand_4 (nand_4_out, not_2_out, not_3_out, not_4_out);
  nand nand_5 (nand_5_out, nand_1_out, nand_2_out);
  nand nand_6 (nand_6_out, nand_3_out, nand_4_out);
  not not_5 (not_5_out, nand_5_out);
  not not_6 (not_6_out, nand_6_out);
  nand nand_7 (F, not_5_out, not_6_out);

  // Notes on the sheet:
  //   7404
  //   13
  //   12
  //   7404
  //   5
  //   6
  //   4
  //   3
  //   1
  //   2
  //   7400
  //   5
  //   6
  //   4
  //   7400
  //   2
  //   3
  //   1
  //   7410
  //   5
  //   6
  //   4
  //   3
  //   7410
  //   12
  //   13
  //   2
  //   1
  //   7400
  //   9
  //   10
  //   7400
  //   12
  //   13
  //   8
  //   9
  //   11
  //   11
  //   7404
  //   8
  //   2
  //   1
  //   7404
  //   10
  //   7400
  //   3
endmodule
