// Logisim project 3.circ as structural Verilog: 1 circuit, main circuit main
module main (
  input  A,
  input  B,
  input  C,
  input  D,
  output F
);

  Multiplexer #(.select(3), .enable("false")) multiplexer_1 (
    .in0(1'b1), .in1(D), .in2(D), .in3(D), .in4(1'b0), .in5(D), .in6(1'b1), .in7(1'b0), .out(F),
    .sel({A, B, C}));
endmodule
