// Logisim project DEC1.circ as structural Verilog: 1 circuit, main circuit main
module main (
  input  A,
  input  B,
  input  C,
  output F
);

  wire decoder_1_out0, decoder_1_out3, decoder_1_out6, decoder_1_out7, or_1_out, or_2_out;

  Decoder #(.select(3), .enable("false")) decoder_1 (
    .out0(decoder_1_out0), .out3(decoder_1_out3), .out6(decoder_1_out6), .out7(decoder_1_out7),
    .sel({C, B, A}));  // open: out1, out2, out4, out5
  or or_1 (or_1_out, decoder_1_out0, decoder_1_out3);
  or or_2 (or_2_out, decoder_1_out6, decoder_1_out7);
  or or_3 (F, or_1_out, or_2_out);

  // Notes on the sheet:
  //   74138
  //   15
  //   12
  //   9
  //   7
  //   1
  //   2
  //   3
  //   7432
  //   5
  //   4
  //   2
  //   1
  //   7432
  //   6
  //   7432
  //   12
  //   13
  //   3
  //   11
endmodule
