// Logisim project 2-4 decoder.circ as structural Verilog: 1 circuit, main circuit main
module main (
  input  s0,
  input  s1,
  output out_3,
  output out_4,
  output out_5,
  output out_6
);

  wire nand_1_out, nand_2_out, nand_3_out, nand_4_out, nand_5_out, nand_6_out;

  nand nand_1 (nand_1_out, s0, s0);
  nand nand_2 (nand_2_out, s1, s1);
  nand nand_3 (nand_3_out, nand_1_out, nand_2_out);
  nand nand_4 (nand_4_out, s0, nand_2_out);
  nand nand_5 (nand_5_out, s1, nand_1_out);
  nand nand_6 (nand_6_out, s1, s0);
  nand nand_7 (out_3, nand_3_out, nand_3_out);
  nand nand_8 (out_4, nand_4_out, nand_4_out);
  nand nand_9 (out_5, nand_5_out, nand_5_out);
  nand nand_10 (out_6, nand_6_out, nand_6_out);
endmodule
