// Logisim project 4-bit.circ as structural Verilog: 2 circuits, main circuit main
module main (
  input  [7:0] in_1,
  input  [7:0] in_2,
  input  TC
);

  wire n4b_1_co;

  _4b u_4b_1 (.T_C(TC), .Co(n4b_1_co));  // open: A3, A2, A1, A0, B3, B2, B1, B0, O3, O2, O1, O0
  _4b u_4b_2 (.T_C(n4b_1_co));  // open: A3, A2, A1, A0, B3, B2, B1, B0, O3, O2, O1, O0, Co
endmodule

module _4b (
  input  A3,
  input  A2,
  input  A1,
  input  A0,
  input  B3,
  input  B2,
  input  B1,
  input  B0,
  input  T_C,
  output O3,
  output O2,
  output O1,
  output O0,
  output Co
);

  wire [3:0] xor_1_out;

  assign xor_1_out = {B3, B2, B1, B0} ^ {4{T_C}};  // XOR_Gate xor_1, 4 bits wide
  Adder #(.width(4)) adder_1 (.a({A3, A2, A1, A0}), .b(xor_1_out), .out({O3, O2, O1, O0}), .cin(T_C), .cout(Co));
endmodule
