// Logisim project adder.circ as structural Verilog: 1 circuit, main circuit main
module main (
  input  [3:0] in_1,
  input  [3:0] in_2,
  input  in_3,
  output [4:0] out_4
);

  wire [3:0] xor_1_out;

  xor xor_1 (xor_1_out[0], in_1[0], in_3);
  xor xor_2 (xor_1_out[1], in_1[1], in_3);
  xor xor_3 (xor_1_out[2], in_1[2], in_3);
  xor xor_4 (xor_1_out[3], in_1[3], in_3);
  Adder #(.width(4)) adder_1 (.a(xor_1_out), .b(in_2), .out(out_4[3:0]), .cin(in_3), .cout(out_4[4]));
endmodule
