// Logisim project shift circuit.circ as structural Verilog: 1 circuit, main circuit main
module main (
  input  select_0_right_1_left,
  input  \input ,
  input  input_2,
  input  input_3,
  input  input_4,
  input  input_5,
  input  input_6,
  input  input_7,
  input  input_8,
  input  input_9,
  input  input_10,
  input  input_11,
  input  input_12,
  input  input_13,
  input  input_14,
  input  input_15,
  input  input_16,
  output \output ,
  output output_2,
  output output_3,
  output output_4,
  output output_5,
  output output_6,
  output output_7,
  output output_8,
  output output_9,
  output output_10,
  output output_11,
  output output_12,
  output out_30,
  output output_13,
  output output_14,
  output out_33
);

  Multiplexer multiplexer_1 (.in0(1'b0), .in1(input_2), .out(\output ), .sel(select_0_right_1_left));  // open: en
  Multiplexer multiplexer_2 (.in0(\input ), .in1(input_3), .out(output_2), .sel(select_0_right_1_left));  // open: en
  Multiplexer multiplexer_3 (.in0(input_2), .in1(input_4), .out(output_3), .sel(select_0_right_1_left));  // open: en
  Multiplexer multiplexer_4 (.in0(input_3), .in1(input_5), .out(output_4), .sel(select_0_right_1_left));  // open: en
  Multiplexer multiplexer_5 (.in0(input_4), .in1(input_6), .out(output_5), .sel(select_0_right_1_left));  // open: en
  Multiplexer multiplexer_6 (.in0(input_5), .in1(input_7), .out(output_6), .sel(select_0_right_1_left));  // open: en
  Multiplexer multiplexer_7 (.in0(input_6), .in1(input_8), .out(output_7), .sel(select_0_right_1_left));  // open: en
  Multiplexer multiplexer_8 (.in0(input_7), .in1(input_9), .out(output_8), .sel(select_0_right_1_left));  // open: en
  Multiplexer multiplexer_9 (.in0(input_8), .in1(input_10), .out(output_9), .sel(select_0_right_1_left));  // open: en
  Multiplexer multiplexer_10 (.in0(input_9), .in1(input_11), .out(output_10), .sel(select_0_right_1_left));  // open: en
  Multiplexer multiplexer_11 (
    .in0(input_10), .in1(input_12), .out(output_11), .sel(select_0_right_1_left));  // open: en
  Multiplexer multiplexer_12 (
    .in0(input_11), .in1(input_13), .out(output_12), .sel(select_0_right_1_left));  // open: en
  Multiplexer multiplexer_13 (.in0(input_12), .in1(input_14), .out(out_30), .sel(select_0_right_1_left));  // open: en
  Multiplexer multiplexer_14 (
    .in0(input_13), .in1(input_15), .out(output_13), .sel(select_0_right_1_left));  // open: en
  Multiplexer multiplexer_15 (
    .in0(input_14), .in1(input_16), .out(output_14), .sel(select_0_right_1_left));  // open: en
  Multiplexer multiplexer_16 (.in0(input_15), .in1(1'b0), .out(out_33), .sel(select_0_right_1_left));  // open: en
endmodule
