// Logisim project 2 li (1).circ as structural Verilog: 1 circuit, main circuit main
module main (
  input  in_1,
  output [2:0] out_2
);

  wire and_1_out, and_2_out, and_3_out, clock_1_out, not_1_out, or_1_out, or_2_out, or_3_out, T2_qn;

  not not_1 (not_1_out, in_1);
  or or_1 (or_1_out, in_1, out_2[0]);
  or or_2 (or_2_out, out_2[1], out_2[2]);
  and and_1 (and_1_out, in_1, T2_qn);
  and and_2 (and_2_out, out_2[0], T2_qn);
  and and_3 (and_3_out, or_1_out, or_2_out);
  Clock clock_1 (.out(clock_1_out));
  or or_3 (or_3_out, and_1_out, and_2_out);
  T_Flip_Flop T2 (.clk(clock_1_out), .T(and_3_out), .Q(out_2[2]), .Qn(T2_qn));  // open: preset, reset, en
  T_Flip_Flop T1 (.clk(clock_1_out), .T(or_3_out), .Q(out_2[1]));  // open: Qn, preset, reset, en
  T_Flip_Flop T0 (.clk(clock_1_out), .T(not_1_out), .Q(out_2[0]));  // open: Qn, preset, reset, en
endmodule
